# Fritzing sketch awt_fritzing (saved by Fritzing 0.9.2b)
circuit board: 4.85083cm x 4.85938cm
perfboards: 1

parts:
  BAT1 = Battery Holders [package=battery-aaa]
  R1 = Resistor [tolerance=±5% resistance=976k package=THT]
  R2 = Resistor [tolerance=±5% resistance=562k package=THT]
  MCP1640 = IC, DIP package, 6 pins
  C1 = Ceramic Capacitor [capacitance=4.7µF package="100 mil [THT, multilayer]"]
  attiny85 = attiny85 [package=dip]
  DHT = Humidity and Temperature Sensor RHT03
  U2 = RF-LINK_TX [package=rf-link_tx]
  C2 = Ceramic Capacitor [capacitance=10µF package="100 mil [THT, multilayer]"]
  R3 = Resistor [tolerance=±5% resistance=220 package=THT]
  R4 = Resistor [tolerance=±5% resistance=220 package=THT]
  LED = LED - 3mm [color="Blue (430nm)" package="3 mm [THT]"]
  R5 = Resistor [tolerance=±5% resistance=220 package=THT]
  L1_4_7μH = Inductors [package=b82462g]
  Reset_Switch = Pushbutton [package=THT]

nets:
  N1: BAT1.-, R2.Pin_1, MCP1640.pin2, C1.1, attiny85.Pin_4, DHT.GND_1, DHT.GND_2, U2.GND, C2.0, R4.Pin_1, Reset_Switch.leg1
  N2: BAT1.+, MCP1640.pin3, MCP1640.pin6, C1.0, L1_4_7μH.2
  N3: R1.Pin_0, R2.Pin_0, MCP1640.pin4
  VCC: R1.Pin_1, MCP1640.pin5, attiny85.Pin_8, DHT.Vcc, U2.+5V, C2.1, R3.Pin_1, R5.Pin_1
  N4: MCP1640.pin1, L1_4_7μH.1
  N5: attiny85.Pin_1, R3.Pin_0, Reset_Switch.leg0
  N6: attiny85.Pin_3, LED.anode
  N7: attiny85.Pin_5, U2.DATA
  N8: attiny85.Pin_6, DHT.Data-signal, R5.Pin_0
  N9: R4.Pin_0, LED.cathode

notes:
  475
  106
  1640
  MCP
  L¹  4.7μH
  Vin=0.7v to 1.7v
